# Fritzing sketch bme280 (saved by Fritzing 0.9.3b)
breadboards: 1

parts:
  U1 = ESP8266 WiFi Module [part_number=ESP8266]
  Part1 = Breadboard Power Supply Board SMD
  C1 = Electrolytic Capacitor [capacitance=1µF package="100 mil [THT, electrolytic]"]
  Part2 = FTDI Basic Programmer
  Part3 = BME280 Breakout

nets:
  N1: U1.RXD, Part2.TXO
  VCC: U1.VCC, U1.GPIO_0, U1.GPIO_2, U1.CH_PD, Part1.VCC, C1.+
  GND: U1.GND, U1.GPIO_15, Part1.GND, C1.-, Part2.GND
  N2: U1.TXD, Part2.RXI
  N3: U1.GPIO_4, Part3.SDI/SDA
  N4: U1.GPIO_5, Part3.SCK/SCL
